# Fritzing sketch blinky-smd_v2 (saved by Fritzing 0.7.12b)
breadboards: 1

parts:
  U1 = 555 Timer [package="SO8 [SMD]"]
  LED1 = smd LED [color="Red (633nm)" package="1206 [SMD]"]
  LED2 = smd LED [color="Red (633nm)" package="1206 [SMD]"]
  R1 = Resistor [tolerance=±5% resistance=1M package="1206 [SMD]"]
  R2 = Resistor [tolerance=±5% resistance=1M package="1206 [SMD]"]
  C1 = Ceramic Capacitor [capacitance=100nF package="1206 [SMD, multilayer]"]
  R3 = Resistor [tolerance=±5% resistance=100 package="1206 [SMD]"]
  R4 = Resistor [tolerance=±5% resistance=100 package="1206 [SMD]"]
  C2 = Ceramic Capacitor [capacitance=10nF package="1206 [SMD, multilayer]"]

nets:
  N1: U1.Pin_1, LED1.cathode, C1.1
  N2: U1.Pin_2, U1.Pin_6, R2.Pin_0, C1.0
  N3: U1.Pin_3, R3.Pin_0, R4.Pin_0
  N4: U1.Pin_4, U1.Pin_8, LED2.anode, R1.Pin_1
  N5: U1.Pin_5, C2.0
  N6: U1.Pin_7, R1.Pin_0, R2.Pin_1
  N7: LED1.anode, R3.Pin_1
  N8: LED2.cathode, R4.Pin_1
