# Fritzing sketch chaser (saved by Fritzing 0.8.0b)
breadboards: 1

parts:
  4017 = IC, DIP package, 16 pins [chip_label=IC]
  9V1 = 9V Battery
  LED1 = LED - 5mm [color="Red (633nm)" package="5 mm [THT]"]
  LED2 = LED - 5mm [color="Red (633nm)" package="5 mm [THT]"]
  LED3 = LED - 5mm [color="Red (633nm)" package="5 mm [THT]"]
  LED4 = LED - 5mm [color="Red (633nm)" package="5 mm [THT]"]
  LED5 = LED - 5mm [color="Red (633nm)" package="5 mm [THT]"]
  LED6 = LED - 5mm [color="Red (633nm)" package="5 mm [THT]"]
  LED7 = LED - 5mm [color="Red (633nm)" package="5 mm [THT]"]
  LED8 = LED - 5mm [color="Red (633nm)" package="5 mm [THT]"]
  LED9 = LED - 5mm [color="Red (633nm)" package="5 mm [THT]"]
  LED10 = LED - 5mm [color="Red (633nm)" package="5 mm [THT]"]
  Flashing = LED - 5mm [color="Red (633nm)" package="5 mm [THT]"]
  R1 = Resistor [tolerance=±5% resistance=1k package=THT]
  R2 = Resistor [tolerance=±5% resistance=470 package=THT]

nets:
  N1: 4017.pin1, LED10.anode
  N2: 4017.pin2, LED9.anode
  N3: 4017.pin3, LED8.anode
  N4: 4017.pin4, LED7.anode
  N5: 4017.pin5, LED6.anode
  N6: 4017.pin6, LED5.anode
  N7: 4017.pin7, LED4.anode
  N8: 4017.pin8, 4017.pin13, 4017.pin15, 9V1.-, R1.Pin_1, R2.Pin_1
  N9: 4017.pin9, LED3.anode
  N10: 4017.pin10, LED2.anode
  N11: 4017.pin11, LED1.anode
  N12: 4017.pin14, Flashing.cathode, R1.Pin_0
  N13: 4017.pin16, 9V1.+, Flashing.anode
  N14: LED1.cathode, LED2.cathode, LED3.cathode, LED4.cathode, LED5.cathode, LED6.cathode, LED7.cathode, LED8.cathode, LED9.cathode, LED10.cathode, R2.Pin_0

custom parts:
  9V Battery: A nine volt battery
